// Digital circuit bola1d.dig as structural Verilog
module bola1d (
  input  relogio,
  input  inicializa,
  input  move,
  input  [11:0] centro,
  input  volta,
  input  reflete,
  input  sobe,
  input  desce,
  output [11:0] posicao
);

  wire and_1_out, and_2_out, or_1_out, or_2_out;
  wire [1:0] or_3_out;
  wire [11:0] add_1_s, add_2_s, multiplexer_1_out, multiplexer_2_out, multiplexer_3_out, neg_1_out, sub_1_s,
       velocidade_q;

  or or_1 (or_1_out, inicializa, move);
  or or_2 (or_2_out, volta, inicializa);
  and and_1 (and_1_out, sobe, reflete);
  and and_2 (and_2_out, desce, reflete);
  Multiplexer #(.Bits(12)) multiplexer_1 (.sel(or_2_out), .in_0(add_1_s), .in_1(centro), .out(multiplexer_1_out));
  or or_3 (or_3_out[0], and_1_out, or_2_out);
  or or_4 (or_3_out[1], and_2_out, or_2_out);
  Register #(.Bits(12)) u_posicao (.D(multiplexer_1_out), .C(relogio), .en(or_1_out), .Q(posicao));
  Register #(.Bits(12)) velocidade (.D(multiplexer_3_out), .C(relogio), .en(or_1_out), .Q(velocidade_q));
  Add #(.Bits(12)) add_1 (.a(posicao), .b(velocidade_q), .s(add_1_s));  // open: c_i, c_o
  Neg #(.Bits(12)) neg_1 (.in(velocidade_q), .out(neg_1_out));
  Multiplexer #(.Bits(12)) multiplexer_2 (
    .sel(reflete), .in_0(velocidade_q), .in_1(neg_1_out), .out(multiplexer_2_out));
  Add #(.Bits(12)) add_2 (.a(multiplexer_2_out), .b(12'h1), .c_i(1'b0), .s(add_2_s));  // open: c_o
  Sub #(.Bits(12)) sub_1 (.a(multiplexer_2_out), .b(12'h1), .c_i(1'b0), .s(sub_1_s));  // open: c_o
  Multiplexer #(.Bits(12), .Selector_Bits(2)) multiplexer_3 (
    .sel(or_3_out), .in_0(multiplexer_2_out), .in_1(add_2_s), .in_2(sub_1_s), .in_3({12{1'b1}}),
    .out(multiplexer_3_out));
endmodule
