// Digital circuit jogador.dig as structural Verilog
module jogador (
  input  relogio,
  input  inicializa,
  input  vs,
  input  sobe1,
  input  desce1,
  input  sobe2,
  input  desce2,
  input  colj1,
  input  colj2,
  output [11:0] bolax,
  output [11:0] bolay,
  output [11:0] j1y,
  output [11:0] j2y,
  output [3:0] digito1,
  output [3:0] digito2,
  output [3:0] digito10,
  output [3:0] digito20
);

  wire and_1_out, and_2_out, and_3_out, d_ff_1_nq;

  D_FF d_ff_1 (.D(vs), .C(relogio), .nQ(d_ff_1_nq));  // open: Q
  and and_1 (and_1_out, vs, d_ff_1_nq);
  and and_2 (and_2_out, sobe1, and_1_out);
  and and_3 (and_3_out, sobe2, and_1_out);
  bola1d bola1d_1 (
    .relogio(relogio), .inicializa(inicializa), .move(and_1_out), .centro(12'h140), .posicao(bolax));  // open: volta, reflete, sobe, desce
  bola1d bola1d_2 (
    .relogio(relogio), .inicializa(inicializa), .move(and_1_out), .centro(12'hf0), .posicao(bolay));  // open: volta, reflete, sobe, desce
  // raquete raquete_1: pin names not known; wires that end beside it: relogio, inicializa, and_1_out, sobe1, desce1, j1y
  // raquete raquete_2: pin names not known; wires that end beside it: relogio, inicializa, and_1_out, sobe2, desce2, j2y
  // placar placar_1: pin names not known; wires that end beside it: relogio, inicializa, and_2_out, digito1, digito10
  // placar placar_2: pin names not known; wires that end beside it: inicializa, relogio, relogio, inicializa, and_3_out, digito2, digito20
endmodule
