// Digital circuit pintor.dig as structural Verilog
module pintor (
  input  [11:0] x,
  input  [11:0] y,
  input  [11:0] bx,
  input  [11:0] by,
  input  [11:0] j1y,
  input  [11:0] j2y,
  input  [3:0] digito1,
  input  [3:0] digito10,
  input  [3:0] digito2,
  input  [3:0] digito20,
  output borda,
  output placar2,
  output jogador2,
  output placar1,
  output jogador1,
  output bola
);

  wire comparator_1_lt, comparator_2_gt, digito_1_p5, digito_2_p5, digito_3_p5, digito_4_p5, retangulo_1_p7;
  wire [11:0] add_1_s, add_2_s, add_3_s, add_4_s, sub_1_s, sub_2_s, sub_3_s, sub_4_s;

  // digito digito_1: pin names not known; wires that end beside it: x, y, digito1, 5'b00110, digito_1_p5
  // digito digito_2: pin names not known; wires that end beside it: x, y, digito10, 5'b00101, digito_2_p5
  // digito digito_3: pin names not known; wires that end beside it: x, y, digito2, 5'b01111, digito_3_p5
  // digito digito_4: pin names not known; wires that end beside it: x, y, digito20, 5'b01110, digito_4_p5
  Sub #(.Bits(12)) sub_1 (.a(bx), .b(12'h6), .c_i(1'b0), .s(sub_1_s));  // open: c_o
  Sub #(.Bits(12)) sub_2 (.a(by), .b(12'h6), .c_i(1'b0), .s(sub_2_s));  // open: c_o
  Sub #(.Bits(12)) sub_3 (.a(j1y), .b(12'h28), .c_i(1'b0), .s(sub_3_s));  // open: c_o
  or or_1 (placar1, digito_1_p5, digito_2_p5);
  or or_2 (placar2, digito_3_p5, digito_4_p5);
  Add #(.Bits(12)) add_1 (.a(bx), .b(12'h6), .c_i(1'b0), .s(add_1_s));  // open: c_o
  Add #(.Bits(12)) add_2 (.a(by), .b(12'h6), .c_i(1'b0), .s(add_2_s));  // open: c_o
  Add #(.Bits(12)) add_3 (.a(j1y), .b(12'h28), .c_i(1'b0), .s(add_3_s));  // open: c_o
  Sub #(.Bits(12)) sub_4 (.a(j2y), .b(12'h28), .c_i(1'b0), .s(sub_4_s));  // open: c_o
  Add #(.Bits(12)) add_4 (.a(j2y), .b(12'h28), .c_i(1'b0), .s(add_4_s));  // open: c_o
  // retangulo retangulo_1: pin names not known; wires that end beside it: x, y, 12'h13c, 12'h144, 12'h1, 12'h1de, retangulo_1_p7
  // retangulo retangulo_2: pin names not known; wires that end beside it: x, y, sub_1_s, add_1_s, sub_2_s, add_2_s, bola
  // retangulo retangulo_3: pin names not known; wires that end beside it: x, y, 12'h20, 12'h2e, sub_3_s, add_3_s, jogador1
  // retangulo retangulo_4: pin names not known; wires that end beside it: x, y, 12'h252, 12'h260, sub_4_s, add_4_s, jogador2
  Comparator #(.Bits(12)) comparator_1 (.a(y), .b(12'h8), .lt(comparator_1_lt));  // open: gt, eq
  Comparator #(.Bits(12)) comparator_2 (.a(y), .b(12'h1d8), .gt(comparator_2_gt));  // open: eq, lt
  or or_3 (borda, comparator_1_lt, retangulo_1_p7, comparator_2_gt);
endmodule
