// Digital circuit placar.dig as structural Verilog
module placar (
  input  relogio,
  input  inicializa,
  input  conta,
  output [3:0] digito1,
  output [3:0] digito10
);

  wire and_1_out;

  Counter #(.Bits(4)) counter_1 (.en(conta), .C(relogio), .clr(and_1_out), .out(digito1));  // open: ovf
  Counter #(.Bits(4)) counter_2 (.en(and_1_out), .C(relogio), .clr(inicializa), .out(digito10));  // open: ovf
  and and_1 (and_1_out, digito1[0], ~digito1[1], ~digito1[2], digito1[3], conta);  // And
  // Pins of 1 and 4 bits meet at digito1
  // Pins of 1 and 4 bits meet at digito10
endmodule
