// Digital circuit temporiza.dig as structural Verilog
// Este bloco gera uma contagem e dois sinais auxiliares que dividem
// a contagem em 4 regioes. O que esta sendo contado eh controlado por
// um sinal "conta" que pode ficar sempre em 1 se for desejado contar
// diretamente ciclos de relogio.
// mostra:  ----------------------------------______________________---
// sinc:    _________________________________________----------________
//       4  |             1                  |  2    |    3    | 4  |  1
// 1) ATIVO
// 2) PRESINC
// 3) LARGURASINC
// 4) POSSINC
// A contagem comeca em zero no  inicio da regiao ativa e deve ser menor
// que o valor maximo do contador (2047 com 11 bits) ateh o fim da regiao 4
module temporiza (
  input  relogio,
  input  conta,
  input  inicializa,
  input  [11:0] upix,
  input  [11:0] inisinc,
  input  [11:0] fimsinc,
  input  [11:0] fimcont,
  output [11:0] contagem,
  output fim,
  output mostra,
  output sinc
);

  wire and_1_out, compara_1_p3, compara_2_p3, compara_3_p3, or_1_out, or_2_out, or_3_out;

  Counter #(.Bits(12)) counter_1 (.en(conta), .C(relogio), .clr(or_3_out), .out(contagem));  // open: ovf
  // compara compara_1: pin names not known; wires that end beside it: contagem, upix, compara_1_p3
  // compara compara_2: pin names not known; wires that end beside it: contagem, inisinc, compara_2_p3
  // compara compara_3: pin names not known; wires that end beside it: contagem, fimsinc, compara_3_p3
  // compara compara_4: pin names not known; wires that end beside it: contagem, fimcont, fim
  or or_1 (or_1_out, compara_1_p3, fim);
  or or_2 (or_2_out, compara_2_p3, compara_3_p3);
  or or_3 (or_3_out, and_1_out, inicializa);
  Register register_1 (.D(fim), .C(relogio), .en(or_1_out), .Q(mostra));
  Register register_2 (.D(compara_2_p3), .C(relogio), .en(or_2_out), .Q(sinc));
  and and_1 (and_1_out, fim, conta);

  // Notes on the sheet:
  //   upix: indica que este é o último pixel visivel ou
  //   a última linha visível
  //   inisinc: indica que o pulso de sincronização deve iniciar
  //   fimsinc: indica que o pulso de sincronização deve terminar
  //   fimcont: inidica que este é a última contagem antes de voltar para zero
endmodule
